# Fritzing sketch pcb-nodemcu_mcp3208 (saved by Fritzing 0.9.3b)
circuit board: 8.1cm x 5.1cm
breadboards: 1

parts:
  IC1 = MCP3208 8-channel 12-bit ADC [part_number=MCP3208]
  U1 = NodeMCU V1.0
  R1 = Resistor [tolerance=±5% resistance=220 package=THT]
  R2 = Resistor [tolerance=±5% resistance=220 package=THT]
  R4 = Resistor [tolerance=±5% resistance=220 package=THT]
  R5 = Resistor [tolerance=±5% resistance=220 package=THT]
  R6 = Resistor [tolerance=±5% resistance=220 package=THT]
  R8 = Resistor [tolerance=±5% resistance=220 package=THT]
  R7 = Resistor [tolerance=±5% resistance=220 package=THT]
  R10 = Resistor [tolerance=±5% resistance=220 package=THT]
  R9 = Resistor [tolerance=±5% resistance=220 package=THT]
  JP14 = Header 12 [package=1x12_machine-pin-header_lock.004]
  J3 = Camdenboss CTB0158-2 [part_number=CTB0158-2 package=THT]
  JP15 = Header 1 [package=1x01_offset]
  JP16 = Header 1 [package=1x01_offset]
  JP17 = Header 1 [package=1x01_offset]
  J2 = Camdenboss CTB0158-10 [part_number=CTB0158-10 package=THT]
  J4 = Camdenboss CTB0158-2 [part_number=CTB0158-2 package=THT]
  J5 = Camdenboss CTB0158-8 [part_number=CTB0158-8 package=THT]
  JP21 = Header 12 [package=1x12_machine-pin-header_lock.004]
  JP22 = Header 12 [package=1x12_machine-pin-header_lock.004]
  JP23 = Header 3 [package=molex-1x3_lock]  # not connected
  JP24 = Header 3 [package=molex-1x3_lock]
  R18 = Resistor [tolerance=±5% resistance=0 package=THT]
  D1 = Zener Diode [part_number=1N4732A breakdown_voltage=3.6V package="300 mil [THT]"]
  D2 = Zener Diode [part_number=1N4732A breakdown_voltage=3.6V package="300 mil [THT]"]
  D3 = Zener Diode [part_number=1N4732A breakdown_voltage=3.6V package="300 mil [THT]"]
  R3 = Resistor [tolerance=±5% resistance=220 package=THT]

nets:
  N1: IC1.1, R1.Pin_0, R2.Pin_0, D1.cathode
  N2: IC1.2, R4.Pin_0, D2.cathode, R3.Pin_0
  N3: IC1.3, R5.Pin_0, R6.Pin_0, D3.cathode
  N4: IC1.4, JP15.1
  N5: IC1.5, JP16.1
  N6: IC1.6, JP17.1
  N7: IC1.7, R7.Pin_1, J2.pin4
  N8: IC1.8, R8.Pin_1, J2.pin3
  N9: IC1.9, IC1.14, U1.GND, R1.Pin_1, R5.Pin_1, R8.Pin_0, R7.Pin_0, JP14.4, J3.pin2, J2.pin6, J2.pin8, J2.pin10, J4.pin2, J5.pin2, J5.pin4, J5.pin6, J5.pin8, JP21.2, D2.anode, D3.anode, R3.Pin_1
  N10: IC1.10, U1.D5
  N11: IC1.11, U1.D6
  N12: IC1.12, U1.D7
  N13: IC1.13, U1.D8
  N14: IC1.15, IC1.16, U1.3V3, JP14.3, J4.pin1, JP22.1
  N15: U1.D2, J5.pin3
  N16: U1.D3, R10.Pin_0
  N17: U1.D4, R9.Pin_0
  N18: U1.Vin, J3.pin1
  N19: U1.RST, JP14.1
  N20: U1.EN, JP14.2
  N21: U1.CLK, JP14.5
  N22: U1.SD0, JP14.6
  N23: U1.CMD, JP14.7
  N24: U1.SD1, JP14.8
  N25: U1.SD2, JP14.9
  N26: U1.SD3, JP14.10
  N27: U1.RSV#40, JP14.11
  N28: U1.RSV#41, JP14.12
  N29: R2.Pin_1, J2.pin9
  N30: R4.Pin_1, J2.pin7
  N31: R6.Pin_1, J2.pin5
  N32: R10.Pin_1, J5.pin5
  N33: R9.Pin_1, J5.pin7
  N34: J2.pin1, J2.pin2, R18.Pin_1
  N35: J5.pin1, JP24.2
  N36: JP22.10, R18.Pin_0

notes:
  Eddy-2-Power
  Charge Controller

custom parts:
  MCP3208 8-channel 12-bit ADC: 12-bit resolution ± 1 LSB max DNL ± 1 LSB max INL (MCP3204/3208-B) ± 2 LSB max INL (MCP3204/3208-C) 4 (MCP3204) or 8 (MCP3208) input channels Analog inputs programmable as single-ended or pseudo differential pairs On-chip sample and hold SPI ® serial interface (modes 0,0 and 1,1) Single supply operation: 2.7V - 5.5V 100ksps max. sampling rate at V DD = 5V 50ksps max. sampling rate at V DD =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
  NodeMCU V1.0: ESP8266 based NodeMCU
