# Fritzing sketch Entladeschutz (saved by Fritzing 0.9.3b)
breadboards: 1

parts:
  U1 = 555 Timer [package="SO8 [SMD]"]
  IC1 = Voltage Regulator [package=to-92]
  D1 = Diode [package=diode-hv]
  U3 = RELAY [package=OJ]
  R2 = Resistor [tolerance=±5% resistance=220 package=THT]
  R4 = Resistor [tolerance=±5% resistance=220 package=THT]
  C1 = Capacitor [package=cap-pth-small2]
  R5 = Resistor [tolerance=±5% resistance=220 package=THT]
  R6 = Resistor [tolerance=±5% resistance=220 package=THT]
  C2 = Electrolytic Capacitor [capacitance=1µF package="100 mil [THT, electrolytic]"]

nets:
  N1: U1.Pin_1, IC1.GND, U3.COIL1, C1.1, R5.Pin_1, R6.Pin_1, C2.+
  N2: U1.Pin_2, R2.Pin_1, R6.Pin_0
  N3: U1.Pin_3, D1.A, U3.COIL2
  N4: U1.Pin_5, C1.2
  N5: U1.Pin_6, R4.Pin_1, R5.Pin_0
  N6: U1.Pin_8, IC1.OUT, D1.C
  N7: IC1.IN, R2.Pin_0, R4.Pin_0, C2.-
